# Fritzing sketch StratoBalloon (saved by Fritzing 0.9.3b)
breadboards: 1
perfboards: 1

parts:
  Grove1 = Grove OLED 128x96  # not connected
  Raspberry_Pi_Zero1 = Raspberry Pi Zero  # not connected
  S1 = Round Pushbutton  # not connected
  U1 = TEMPERATURE-SENSOR [package=to-92]  # not connected
  R1 = Resistor [tolerance=±5% resistance=220 package=THT]  # not connected
  S2 = Pushbutton [package="[THT]"]
  RHT1 = Humidity and Temperature Sensor RHT03  # not connected
  VCC1 = Battery  # not connected
  J1 = shrouded pin header, 40 pins [form="♂ (shrouded male)"]  # not connected
  LED1 = LED - 3mm [color="Red (633nm)" package="3 mm [THT]"]  # not connected
  LED2 = LED - 3mm [color="Red (633nm)" package="3 mm [THT]"]  # not connected

nets:
  N1: S2.Pin_1, S2.Pin_2
  N2: S2.Pin_3, S2.Pin_4
